# Fritzing sketch voltage_sensor_uno (saved by Fritzing 0.9.4)
breadboards: 1

parts:
  Part1 = Arduino Uno (Rev3) - ICSP
  Part2 = Voltage Sensor 25V

nets:
  N1: Part1.A0, Part2.S
  N2: Part1.GND, Part2.-
